// Logisim project circuito.circ as structural Verilog
module BC (
  input  inicio,
  input  zero,
  input  clk,
  input  rst,
  output set,
  output rac,
  output dec,
  output cac,
  output pronto
);

  wire and_1_out, and_2_out, and_3_out, and_4_out, and_5_out, d_ff_1_q, d_ff_2_q, or_1_out;

  and and_1 (and_1_out, d_ff_1_q, ~d_ff_2_q);  // AND_Gate
  and and_2 (and_2_out, ~d_ff_1_q, d_ff_2_q, zero);  // AND_Gate
  and and_3 (and_3_out, inicio, ~d_ff_2_q);  // AND_Gate
  and and_4 (and_4_out, inicio, zero);
  and and_5 (and_5_out, ~d_ff_2_q, d_ff_1_q);  // AND_Gate
  or or_1 (or_1_out, and_1_out, and_2_out, and_3_out, and_4_out);
  D_Flip_Flop d_ff_1 (.D(and_5_out), .clk(clk), .Q(d_ff_1_q), .reset(rst));  // open: Qn, preset
  D_Flip_Flop d_ff_2 (.D(or_1_out), .clk(clk), .Q(d_ff_2_q), .reset(rst));  // open: Qn, preset
  and and_6 (rac, ~d_ff_1_q, ~d_ff_2_q);  // AND_Gate
  and and_7 (cac, d_ff_1_q, ~d_ff_2_q);  // AND_Gate
  xnor xnor_1 (pronto, d_ff_1_q, d_ff_2_q);

  assign dec = cac;
  assign set = rac;
endmodule

module BO (
  input  clk,
  input  rst,
  input  dec,
  input  set,
  input  cac,
  input  rac,
  input  [7:0] valor,
  output zero,
  output overflow,
  output [7:0] soma
);

  wire [7:0] adder_1_out;

  Adder adder_1 (.a(valor), .b(soma), .out(adder_1_out), .cout(overflow));  // open: cin
  Register register_1 (.en(set));  // open: D, clk, Q, clr
endmodule
